# Fritzing sketch main-board (saved by Fritzing 0.8.3b)
circuit board: 16.9333cm x 5.64444cm
perfboards: 1

parts:
  J1 = shrouded pin header, 10 pins [form="♂ (shrouded male)"]
  J2 = shrouded pin header, 10 pins [form="♂ (shrouded male)"]
  J3 = shrouded pin header, 10 pins [form="♂ (shrouded male)"]
  パーツ1 = Arduino Uno (Rev3)

nets:
  N1: J1.pin2, J2.pin2, J3.pin2
  N2: J1.pin3, J2.pin3, J3.pin3
  N3: J1.pin4, パーツ1.D9_PWM
  N4: J1.pin6, J2.pin6, J3.pin6, パーツ1.D6_PWM
  N5: J1.pin7, J2.pin7, J3.pin7
  N6: J1.pin8, J2.pin8, J3.pin8, パーツ1.D11_PWM/MOSI
  N7: J1.pin9, J2.pin9, J3.pin9
  N8: J2.pin4, パーツ1.D8
  N9: J3.pin4, パーツ1.D7
